// Logisim project Tarea2_CircSecuencial.circ as structural Verilog: 8 circuits, main circuit main
module main (
  input  [3:0] in_1,
  input  in_2,
  input  in_3,
  input  in_4,
  input  in_5,
  input  in_6,
  input  in_7,
  input  in_8,
  input  in_9,
  input  in_10,
  input  in_11,
  input  in_12,
  input  in_13,
  input  in_14,
  input  in_15,
  input  in_16,
  input  in_17,
  input  in_18,
  input  in_19,
  input  in_20,
  input  in_21,
  input  in_22,
  input  in_23,
  input  in_24,
  input  in_25,
  input  in_26,
  input  in_27,
  input  in_28,
  input  in_29,
  input  in_30,
  input  in_31,
  input  in_32,
  input  in_33,
  input  in_34,
  input  in_35,
  input  in_36,
  input  in_37,
  input  in_38,
  input  in_39,
  input  in_40,
  input  in_41,
  input  in_42,
  input  in_43,
  input  in_44,
  input  in_45,
  input  in_46,
  input  in_47,
  input  in_48,
  input  in_49,
  input  in_50,
  input  in_51,
  input  in_52,
  input  in_53,
  input  in_54,
  input  in_55,
  input  in_56,
  input  in_57,
  input  in_58,
  input  in_59,
  input  in_60,
  input  in_61,
  input  in_62,
  input  in_63,
  input  in_64,
  input  in_65,
  input  in_66,
  input  in_67,
  input  in_68,
  input  in_69,
  input  in_70,
  input  in_71,
  input  in_72,
  input  in_73,
  input  in_74,
  input  in_75,
  input  in_76,
  input  in_77,
  input  in_78,
  input  in_79,
  input  in_80,
  input  in_81,
  input  in_82,
  input  in_83,
  input  in_84,
  input  in_85,
  input  in_86,
  input  in_87,
  input  in_88,
  input  in_89,
  input  in_90,
  input  in_91,
  output L,
  output F,
  output R,
  output L_2,
  output F_2,
  output R_2,
  output L_3,
  output F_3,
  output R_3,
  output L_4,
  output F_4,
  output R_4,
  output L_5,
  output F_5,
  output R_5,
  output L_6,
  output F_6,
  output R_6,
  output L_7,
  output F_7,
  output R_7,
  output L_8,
  output F_8,
  output R_8,
  output L_9,
  output F_9,
  output R_9,
  output L_10,
  output F_10,
  output R_10,
  output L_11,
  output F_11,
  output R_11,
  output L_12,
  output F_12,
  output R_12,
  output L_13,
  output F_13,
  output R_13,
  output L_14,
  output F_14,
  output R_14,
  output D3,
  output D2,
  output D1,
  output D0,
  output L_15,
  output F_15,
  output R_15
);

  wire circuito_combi_1_d0, circuito_combi_1_d1, circuito_combi_1_d2, circuito_combi_1_d3,
       circuito_combi_2_d0, circuito_combi_2_d1, circuito_combi_2_d2, circuito_combi_2_d3,
       circuito_combi_3_d0, circuito_combi_3_d1, circuito_combi_3_d2, circuito_combi_3_d3,
       circuito_combi_4_d0, circuito_combi_4_d1, circuito_combi_4_d2, circuito_combi_4_d3,
       circuito_combi_5_d0, circuito_combi_5_d1, circuito_combi_5_d2, circuito_combi_5_d3,
       circuito_combi_6_d0, circuito_combi_6_d1, circuito_combi_6_d2, circuito_combi_6_d3,
       circuito_combi_7_d0, circuito_combi_7_d1, circuito_combi_7_d2, circuito_combi_7_d3,
       circuito_combi_8_d0, circuito_combi_8_d1, circuito_combi_8_d2, circuito_combi_8_d3,
       circuito_combi_9_d0, circuito_combi_9_d1, circuito_combi_9_d2, circuito_combi_9_d3,
       circuito_combi_10_d0, circuito_combi_10_d1, circuito_combi_10_d2, circuito_combi_10_d3,
       circuito_combi_11_d0, circuito_combi_11_d1, circuito_combi_11_d2, circuito_combi_11_d3,
       circuito_combi_12_d0, circuito_combi_12_d1, circuito_combi_12_d2, circuito_combi_12_d3,
       circuito_combi_13_d0, circuito_combi_13_d1, circuito_combi_13_d2, circuito_combi_13_d3,
       circuito_combi_14_d0, circuito_combi_14_d1, circuito_combi_14_d2, circuito_combi_14_d3, CLOCK_out,
       n6_bit_register_1_q0, n6_bit_register_1_q1, n6_bit_register_1_q2, n6_bit_register_1_q3,
       n6_bit_register_1_q4, n6_bit_register_1_q5, n6_bit_register_2_q0, n6_bit_register_2_q1,
       n6_bit_register_2_q2, n6_bit_register_2_q3, n6_bit_register_2_q4, n6_bit_register_2_q5,
       n6_bit_register_3_q0, n6_bit_register_3_q1, n6_bit_register_3_q2, n6_bit_register_3_q3,
       n6_bit_register_3_q4, n6_bit_register_3_q5, n6_bit_register_4_q0, n6_bit_register_4_q1,
       n6_bit_register_4_q2, n6_bit_register_4_q3, n6_bit_register_4_q4, n6_bit_register_4_q5,
       n6_bit_register_5_q0, n6_bit_register_5_q1, n6_bit_register_5_q2, n6_bit_register_5_q3,
       n6_bit_register_5_q4, n6_bit_register_5_q5, n6_bit_register_6_q0, n6_bit_register_6_q1,
       n6_bit_register_6_q2, n6_bit_register_6_q3, n6_bit_register_6_q4, n6_bit_register_6_q5,
       n6_bit_register_7_q0, n6_bit_register_7_q1, n6_bit_register_7_q2, n6_bit_register_7_q3,
       n6_bit_register_7_q4, n6_bit_register_7_q5, n6_bit_register_8_q0, n6_bit_register_8_q1,
       n6_bit_register_8_q2, n6_bit_register_8_q3, n6_bit_register_8_q4, n6_bit_register_8_q5,
       n6_bit_register_9_q0, n6_bit_register_9_q1, n6_bit_register_9_q2, n6_bit_register_9_q3,
       n6_bit_register_9_q4, n6_bit_register_9_q5, n6_bit_register_10_q0, n6_bit_register_10_q1,
       n6_bit_register_10_q2, n6_bit_register_10_q3, n6_bit_register_10_q4, n6_bit_register_10_q5,
       n6_bit_register_11_q0, n6_bit_register_11_q1, n6_bit_register_11_q2, n6_bit_register_11_q3,
       n6_bit_register_11_q4, n6_bit_register_11_q5, n6_bit_register_12_q0, n6_bit_register_12_q1,
       n6_bit_register_12_q2, n6_bit_register_12_q3, n6_bit_register_12_q4, n6_bit_register_12_q5,
       n6_bit_register_13_q0, n6_bit_register_13_q1, n6_bit_register_13_q2, n6_bit_register_13_q3,
       n6_bit_register_13_q4, n6_bit_register_13_q5, n6_bit_register_14_q0, n6_bit_register_14_q1,
       n6_bit_register_14_q2, n6_bit_register_14_q3, n6_bit_register_14_q4, n6_bit_register_14_q5,
       n6_bit_register_15_q0, n6_bit_register_15_q1, n6_bit_register_15_q2, n6_bit_register_15_q3,
       n6_bit_register_15_q4, n6_bit_register_15_q5;

  Clock CLOCK (.out(CLOCK_out));
  _6_bit_Register u_6_bit_register_1 (
    .CLK(CLOCK_out), .D0(in_2), .D1(in_3), .D2(in_4), .D3(in_5), .D4(in_6), .D5(in_7),
    .Q0(n6_bit_register_1_q0), .Q1(n6_bit_register_1_q1), .Q2(n6_bit_register_1_q2),
    .Q3(n6_bit_register_1_q3), .Q4(n6_bit_register_1_q4), .Q5(n6_bit_register_1_q5));
  _6_bit_Register u_6_bit_register_2 (
    .CLK(CLOCK_out), .D0(in_8), .D1(in_9), .D2(in_10), .D3(in_11), .D4(in_12), .D5(in_13),
    .Q0(n6_bit_register_2_q0), .Q1(n6_bit_register_2_q1), .Q2(n6_bit_register_2_q2),
    .Q3(n6_bit_register_2_q3), .Q4(n6_bit_register_2_q4), .Q5(n6_bit_register_2_q5));
  _6_bit_Register u_6_bit_register_3 (
    .CLK(CLOCK_out), .D0(in_14), .D1(in_15), .D2(in_16), .D3(in_17), .D4(in_18), .D5(in_19),
    .Q0(n6_bit_register_3_q0), .Q1(n6_bit_register_3_q1), .Q2(n6_bit_register_3_q2),
    .Q3(n6_bit_register_3_q3), .Q4(n6_bit_register_3_q4), .Q5(n6_bit_register_3_q5));
  _6_bit_Register u_6_bit_register_4 (
    .CLK(CLOCK_out), .D0(in_20), .D1(in_21), .D2(in_22), .D3(in_23), .D4(in_24), .D5(in_25),
    .Q0(n6_bit_register_4_q0), .Q1(n6_bit_register_4_q1), .Q2(n6_bit_register_4_q2),
    .Q3(n6_bit_register_4_q3), .Q4(n6_bit_register_4_q4), .Q5(n6_bit_register_4_q5));
  _6_bit_Register u_6_bit_register_5 (
    .CLK(CLOCK_out), .D0(in_26), .D1(in_27), .D2(in_28), .D3(in_29), .D4(in_30), .D5(in_31),
    .Q0(n6_bit_register_5_q0), .Q1(n6_bit_register_5_q1), .Q2(n6_bit_register_5_q2),
    .Q3(n6_bit_register_5_q3), .Q4(n6_bit_register_5_q4), .Q5(n6_bit_register_5_q5));
  _6_bit_Register u_6_bit_register_6 (
    .CLK(CLOCK_out), .D0(in_32), .D1(in_33), .D2(in_34), .D3(in_35), .D4(in_36), .D5(in_37),
    .Q0(n6_bit_register_6_q0), .Q1(n6_bit_register_6_q1), .Q2(n6_bit_register_6_q2),
    .Q3(n6_bit_register_6_q3), .Q4(n6_bit_register_6_q4), .Q5(n6_bit_register_6_q5));
  _6_bit_Register u_6_bit_register_7 (
    .CLK(CLOCK_out), .D0(in_38), .D1(in_39), .D2(in_40), .D3(in_41), .D4(in_42), .D5(in_43),
    .Q0(n6_bit_register_7_q0), .Q1(n6_bit_register_7_q1), .Q2(n6_bit_register_7_q2),
    .Q3(n6_bit_register_7_q3), .Q4(n6_bit_register_7_q4), .Q5(n6_bit_register_7_q5));
  _6_bit_Register u_6_bit_register_8 (
    .CLK(CLOCK_out), .D0(in_44), .D1(in_45), .D2(in_46), .D3(in_47), .D4(in_48), .D5(in_49),
    .Q0(n6_bit_register_8_q0), .Q1(n6_bit_register_8_q1), .Q2(n6_bit_register_8_q2),
    .Q3(n6_bit_register_8_q3), .Q4(n6_bit_register_8_q4), .Q5(n6_bit_register_8_q5));
  _6_bit_Register u_6_bit_register_9 (
    .CLK(CLOCK_out), .D0(in_50), .D1(in_51), .D2(in_52), .D3(in_53), .D4(in_54), .D5(in_55),
    .Q0(n6_bit_register_9_q0), .Q1(n6_bit_register_9_q1), .Q2(n6_bit_register_9_q2),
    .Q3(n6_bit_register_9_q3), .Q4(n6_bit_register_9_q4), .Q5(n6_bit_register_9_q5));
  _6_bit_Register u_6_bit_register_10 (
    .CLK(CLOCK_out), .D0(in_56), .D1(in_57), .D2(in_58), .D3(in_59), .D4(in_60), .D5(in_61),
    .Q0(n6_bit_register_10_q0), .Q1(n6_bit_register_10_q1), .Q2(n6_bit_register_10_q2),
    .Q3(n6_bit_register_10_q3), .Q4(n6_bit_register_10_q4), .Q5(n6_bit_register_10_q5));
  _6_bit_Register u_6_bit_register_11 (
    .CLK(CLOCK_out), .D0(in_62), .D1(in_63), .D2(in_64), .D3(in_65), .D4(in_66), .D5(in_67),
    .Q0(n6_bit_register_11_q0), .Q1(n6_bit_register_11_q1), .Q2(n6_bit_register_11_q2),
    .Q3(n6_bit_register_11_q3), .Q4(n6_bit_register_11_q4), .Q5(n6_bit_register_11_q5));
  _6_bit_Register u_6_bit_register_12 (
    .CLK(CLOCK_out), .D0(in_68), .D1(in_69), .D2(in_70), .D3(in_71), .D4(in_72), .D5(in_73),
    .Q0(n6_bit_register_12_q0), .Q1(n6_bit_register_12_q1), .Q2(n6_bit_register_12_q2),
    .Q3(n6_bit_register_12_q3), .Q4(n6_bit_register_12_q4), .Q5(n6_bit_register_12_q5));
  _6_bit_Register u_6_bit_register_13 (
    .CLK(CLOCK_out), .D0(in_74), .D1(in_75), .D2(in_76), .D3(in_77), .D4(in_78), .D5(in_79),
    .Q0(n6_bit_register_13_q0), .Q1(n6_bit_register_13_q1), .Q2(n6_bit_register_13_q2),
    .Q3(n6_bit_register_13_q3), .Q4(n6_bit_register_13_q4), .Q5(n6_bit_register_13_q5));
  _6_bit_Register u_6_bit_register_14 (
    .CLK(CLOCK_out), .D0(in_80), .D1(in_81), .D2(in_82), .D3(in_83), .D4(in_84), .D5(in_85),
    .Q0(n6_bit_register_14_q0), .Q1(n6_bit_register_14_q1), .Q2(n6_bit_register_14_q2),
    .Q3(n6_bit_register_14_q3), .Q4(n6_bit_register_14_q4), .Q5(n6_bit_register_14_q5));
  _6_bit_Register u_6_bit_register_15 (
    .CLK(CLOCK_out), .D0(in_86), .D1(in_87), .D2(in_88), .D3(in_89), .D4(in_90), .D5(in_91),
    .Q0(n6_bit_register_15_q0), .Q1(n6_bit_register_15_q1), .Q2(n6_bit_register_15_q2),
    .Q3(n6_bit_register_15_q3), .Q4(n6_bit_register_15_q4), .Q5(n6_bit_register_15_q5));
  Circuito_combi circuito_combi_1 (
    .El(n6_bit_register_1_q0), .Er(n6_bit_register_1_q1), .Ef(n6_bit_register_1_q2),
    .Cl(n6_bit_register_1_q3), .B(in_1), .Cr(n6_bit_register_1_q4), .Cf(n6_bit_register_1_q5), .mux(1'b1),
    .D3(circuito_combi_1_d3), .D2(circuito_combi_1_d2), .D1(circuito_combi_1_d1), .D0(circuito_combi_1_d0),
    .L(L), .R(R), .F(F));  // open: A3, A2, A1, A0
  Circuito_combi circuito_combi_2 (
    .A3(circuito_combi_1_d3), .A2(circuito_combi_1_d2), .A1(circuito_combi_1_d1), .A0(circuito_combi_1_d0),
    .El(n6_bit_register_2_q0), .Er(n6_bit_register_2_q1), .Ef(n6_bit_register_2_q2),
    .Cl(n6_bit_register_2_q3), .Cr(n6_bit_register_2_q4), .Cf(n6_bit_register_2_q5), .mux(1'b0),
    .D3(circuito_combi_2_d3), .D2(circuito_combi_2_d2), .D1(circuito_combi_2_d1), .D0(circuito_combi_2_d0),
    .L(L_2), .R(R_2), .F(F_2));  // open: B
  Circuito_combi circuito_combi_3 (
    .A3(circuito_combi_2_d3), .A2(circuito_combi_2_d2), .A1(circuito_combi_2_d1), .A0(circuito_combi_2_d0),
    .El(n6_bit_register_3_q0), .Er(n6_bit_register_3_q1), .Ef(n6_bit_register_3_q2),
    .Cl(n6_bit_register_3_q3), .Cr(n6_bit_register_3_q4), .Cf(n6_bit_register_3_q5), .mux(1'b0),
    .D3(circuito_combi_3_d3), .D2(circuito_combi_3_d2), .D1(circuito_combi_3_d1), .D0(circuito_combi_3_d0),
    .L(L_3), .R(R_3), .F(F_3));  // open: B
  Circuito_combi circuito_combi_4 (
    .A3(circuito_combi_3_d3), .A2(circuito_combi_3_d2), .A1(circuito_combi_3_d1), .A0(circuito_combi_3_d0),
    .El(n6_bit_register_4_q0), .Er(n6_bit_register_4_q1), .Ef(n6_bit_register_4_q2),
    .Cl(n6_bit_register_4_q3), .Cr(n6_bit_register_4_q4), .Cf(n6_bit_register_4_q5), .mux(1'b0),
    .D3(circuito_combi_4_d3), .D2(circuito_combi_4_d2), .D1(circuito_combi_4_d1), .D0(circuito_combi_4_d0),
    .L(L_4), .R(R_4), .F(F_4));  // open: B
  Circuito_combi circuito_combi_5 (
    .A3(circuito_combi_4_d3), .A2(circuito_combi_4_d2), .A1(circuito_combi_4_d1), .A0(circuito_combi_4_d0),
    .El(n6_bit_register_5_q0), .Er(n6_bit_register_5_q1), .Ef(n6_bit_register_5_q2),
    .Cl(n6_bit_register_5_q3), .Cr(n6_bit_register_5_q4), .Cf(n6_bit_register_5_q5), .mux(1'b0),
    .D3(circuito_combi_5_d3), .D2(circuito_combi_5_d2), .D1(circuito_combi_5_d1), .D0(circuito_combi_5_d0),
    .L(L_5), .R(R_5), .F(F_5));  // open: B
  Circuito_combi circuito_combi_6 (
    .A3(circuito_combi_5_d3), .A2(circuito_combi_5_d2), .A1(circuito_combi_5_d1), .A0(circuito_combi_5_d0),
    .El(n6_bit_register_6_q0), .Er(n6_bit_register_6_q1), .Ef(n6_bit_register_6_q2),
    .Cl(n6_bit_register_6_q3), .Cr(n6_bit_register_6_q4), .Cf(n6_bit_register_6_q5), .mux(1'b0),
    .D3(circuito_combi_6_d3), .D2(circuito_combi_6_d2), .D1(circuito_combi_6_d1), .D0(circuito_combi_6_d0),
    .L(L_6), .R(R_6), .F(F_6));  // open: B
  Circuito_combi circuito_combi_7 (
    .A3(circuito_combi_6_d3), .A2(circuito_combi_6_d2), .A1(circuito_combi_6_d1), .A0(circuito_combi_6_d0),
    .El(n6_bit_register_7_q0), .Er(n6_bit_register_7_q1), .Ef(n6_bit_register_7_q2),
    .Cl(n6_bit_register_7_q3), .Cr(n6_bit_register_7_q4), .Cf(n6_bit_register_7_q5), .mux(1'b0),
    .D3(circuito_combi_7_d3), .D2(circuito_combi_7_d2), .D1(circuito_combi_7_d1), .D0(circuito_combi_7_d0),
    .L(L_7), .R(R_7), .F(F_7));  // open: B
  Circuito_combi circuito_combi_8 (
    .A3(circuito_combi_7_d3), .A2(circuito_combi_7_d2), .A1(circuito_combi_7_d1), .A0(circuito_combi_7_d0),
    .El(n6_bit_register_8_q0), .Er(n6_bit_register_8_q1), .Ef(n6_bit_register_8_q2),
    .Cl(n6_bit_register_8_q3), .Cr(n6_bit_register_8_q4), .Cf(n6_bit_register_8_q5), .mux(1'b0),
    .D3(circuito_combi_8_d3), .D2(circuito_combi_8_d2), .D1(circuito_combi_8_d1), .D0(circuito_combi_8_d0),
    .L(L_8), .R(R_8), .F(F_8));  // open: B
  Circuito_combi circuito_combi_9 (
    .A3(circuito_combi_8_d3), .A2(circuito_combi_8_d2), .A1(circuito_combi_8_d1), .A0(circuito_combi_8_d0),
    .El(n6_bit_register_9_q0), .Er(n6_bit_register_9_q1), .Ef(n6_bit_register_9_q2),
    .Cl(n6_bit_register_9_q3), .Cr(n6_bit_register_9_q4), .Cf(n6_bit_register_9_q5), .mux(1'b0),
    .D3(circuito_combi_9_d3), .D2(circuito_combi_9_d2), .D1(circuito_combi_9_d1), .D0(circuito_combi_9_d0),
    .L(L_9), .R(R_9), .F(F_9));  // open: B
  Circuito_combi circuito_combi_10 (
    .A3(circuito_combi_9_d3), .A2(circuito_combi_9_d2), .A1(circuito_combi_9_d1), .A0(circuito_combi_9_d0),
    .El(n6_bit_register_10_q0), .Er(n6_bit_register_10_q1), .Ef(n6_bit_register_10_q2),
    .Cl(n6_bit_register_10_q3), .Cr(n6_bit_register_10_q4), .Cf(n6_bit_register_10_q5), .mux(1'b0),
    .D3(circuito_combi_10_d3), .D2(circuito_combi_10_d2), .D1(circuito_combi_10_d1),
    .D0(circuito_combi_10_d0), .L(L_10), .R(R_10), .F(F_10));  // open: B
  Circuito_combi circuito_combi_11 (
    .A3(circuito_combi_10_d3), .A2(circuito_combi_10_d2), .A1(circuito_combi_10_d1),
    .A0(circuito_combi_10_d0), .El(n6_bit_register_11_q0), .Er(n6_bit_register_11_q1),
    .Ef(n6_bit_register_11_q2), .Cl(n6_bit_register_11_q3), .Cr(n6_bit_register_11_q4),
    .Cf(n6_bit_register_11_q5), .mux(1'b0), .D3(circuito_combi_11_d3), .D2(circuito_combi_11_d2),
    .D1(circuito_combi_11_d1), .D0(circuito_combi_11_d0), .L(L_11), .R(R_11), .F(F_11));  // open: B
  Circuito_combi circuito_combi_12 (
    .A3(circuito_combi_11_d3), .A2(circuito_combi_11_d2), .A1(circuito_combi_11_d1),
    .A0(circuito_combi_11_d0), .El(n6_bit_register_12_q0), .Er(n6_bit_register_12_q1),
    .Ef(n6_bit_register_12_q2), .Cl(n6_bit_register_12_q3), .Cr(n6_bit_register_12_q4),
    .Cf(n6_bit_register_12_q5), .mux(1'b0), .D3(circuito_combi_12_d3), .D2(circuito_combi_12_d2),
    .D1(circuito_combi_12_d1), .D0(circuito_combi_12_d0), .L(L_12), .R(R_12), .F(F_12));  // open: B
  Circuito_combi circuito_combi_13 (
    .A3(circuito_combi_12_d3), .A2(circuito_combi_12_d2), .A1(circuito_combi_12_d1),
    .A0(circuito_combi_12_d0), .El(n6_bit_register_13_q0), .Er(n6_bit_register_13_q1),
    .Ef(n6_bit_register_13_q2), .Cl(n6_bit_register_13_q3), .Cr(n6_bit_register_13_q4),
    .Cf(n6_bit_register_13_q5), .mux(1'b0), .D3(circuito_combi_13_d3), .D2(circuito_combi_13_d2),
    .D1(circuito_combi_13_d1), .D0(circuito_combi_13_d0), .L(L_13), .R(R_13), .F(F_13));  // open: B
  Circuito_combi circuito_combi_14 (
    .A3(circuito_combi_13_d3), .A2(circuito_combi_13_d2), .A1(circuito_combi_13_d1),
    .A0(circuito_combi_13_d0), .El(n6_bit_register_14_q0), .Er(n6_bit_register_14_q1),
    .Ef(n6_bit_register_14_q2), .Cl(n6_bit_register_14_q3), .Cr(n6_bit_register_14_q4),
    .Cf(n6_bit_register_14_q5), .mux(1'b0), .D3(circuito_combi_14_d3), .D2(circuito_combi_14_d2),
    .D1(circuito_combi_14_d1), .D0(circuito_combi_14_d0), .L(L_14), .R(R_14), .F(F_14));  // open: B
  Circuito_combi circuito_combi_15 (
    .A3(circuito_combi_14_d3), .A2(circuito_combi_14_d2), .A1(circuito_combi_14_d1),
    .A0(circuito_combi_14_d0), .El(n6_bit_register_15_q0), .Er(n6_bit_register_15_q1),
    .Ef(n6_bit_register_15_q2), .Cl(n6_bit_register_15_q3), .Cr(n6_bit_register_15_q4),
    .Cf(n6_bit_register_15_q5), .mux(1'b0), .D3(D3), .D2(D2), .D1(D1), .D0(D0), .L(L_15), .R(R_15), .F(F_15));  // open: B

  // Notes on the sheet:
  //   Batería final
endmodule

// SR LATCH
module SR_Latch (
  input  R,
  input  S,
  output Q,
  output nQ
);

  nor nor_1 (Q, R, nQ);
  nor nor_2 (nQ, Q, S);
endmodule

// D LATCH
module D_Latch (
  input  CLK,
  input  D,
  output Q,
  output nQ
);

  wire and_1_out, and_2_out, not_1_out;

  not not_1 (not_1_out, D);
  and and_1 (and_1_out, CLK, not_1_out);
  and and_2 (and_2_out, CLK, D);
  SR_Latch sr_latch_1 (.R(and_1_out), .S(and_2_out), .Q(Q), .nQ(nQ));
endmodule

// D flipflop
module D_Flip_Flop (
  input  CLK,
  input  D,
  output Q,
  output nQ
);

  wire d_latch_1_q, not_1_out;

  not not_1 (not_1_out, CLK);
  D_Latch d_latch_1 (.CLK(not_1_out), .D(D), .Q(d_latch_1_q));  // open: nQ
  D_Latch d_latch_2 (.CLK(CLK), .D(d_latch_1_q), .Q(Q), .nQ(nQ));
endmodule

module _6_bit_Register (
  input  CLK,
  input  D0,
  input  D1,
  input  D2,
  input  D3,
  input  D4,
  input  D5,
  output Q0,
  output Q1,
  output Q2,
  output Q3,
  output Q4,
  output Q5
);

  D_Flip_Flop d_flip_flop_1 (.CLK(CLK), .D(D0), .Q(Q0));  // open: nQ
  D_Flip_Flop d_flip_flop_2 (.CLK(CLK), .D(D1), .Q(Q1));  // open: nQ
  D_Flip_Flop d_flip_flop_3 (.CLK(CLK), .D(D2), .Q(Q2));  // open: nQ
  D_Flip_Flop d_flip_flop_4 (.CLK(CLK), .D(D3), .Q(Q3));  // open: nQ
  D_Flip_Flop d_flip_flop_5 (.CLK(CLK), .D(D4), .Q(Q4));  // open: nQ
  D_Flip_Flop d_flip_flop_6 (.CLK(CLK), .D(D5), .Q(Q5));  // open: nQ
endmodule

// RESTADOR1
module BATERIA (
  input  Carga,
  input  B3,
  input  B2,
  input  B1,
  input  B0,
  output C3,
  output C2,
  output C1,
  output C0
);

  wire and_1_out, and_2_out, and_3_out, and_4_out, and_5_out, and_6_out, and_7_out, and_8_out, and_9_out,
       and_10_out, and_11_out, and_12_out, not_1_out, not_2_out, not_3_out, not_4_out, not_5_out, not_6_out,
       not_7_out, not_8_out, not_9_out, not_10_out;

  and and_1 (and_1_out, B3, B0);
  and and_2 (and_2_out, B3, B1);
  and and_3 (and_3_out, B3, B2);
  not not_1 (not_1_out, B2);
  not not_2 (not_2_out, B1);
  not not_3 (not_3_out, B0);
  not not_4 (not_4_out, B1);
  not not_5 (not_5_out, B0);
  not not_6 (not_6_out, B1);
  not not_7 (not_7_out, B0);
  not not_8 (not_8_out, B0);
  not not_9 (not_9_out, B0);
  not not_10 (not_10_out, B0);
  or or_1 (C3, and_1_out, and_2_out, and_3_out, Carga);
  and and_4 (and_4_out, B2, B0);
  and and_5 (and_5_out, B2, B1);
  and and_6 (and_6_out, B3, not_1_out, not_2_out, not_3_out);
  and and_7 (and_7_out, B1, B0);
  and and_8 (and_8_out, B2, not_4_out, not_5_out);
  and and_9 (and_9_out, B3, not_6_out, not_7_out);
  and and_10 (and_10_out, B1, not_8_out);
  and and_11 (and_11_out, B2, not_9_out);
  and and_12 (and_12_out, B3, not_10_out);
  or or_2 (C2, and_4_out, and_5_out, and_6_out, Carga);
  or or_3 (C1, and_7_out, and_8_out, and_9_out, Carga);
  or or_4 (C0, and_10_out, and_11_out, and_12_out, Carga);
endmodule

module Circuito_combi (
  input  A3,
  input  A2,
  input  A1,
  input  A0,
  input  mux,
  input  El,
  input  Er,
  input  Ef,
  input  Cl,
  input  [3:0] B,
  input  Cr,
  input  Cf,
  output D3,
  output D2,
  output D1,
  output D0,
  output L,
  output R,
  output F
);

  wire and_1_out, and_2_out, and_3_out, and_4_out, and_5_out, and_6_out, and_7_out, and_8_out, and_9_out,
       and_10_out, and_11_out, and_12_out, and_13_out, bitselector_1_out, bitselector_2_out,
       bitselector_3_out, bitselector_4_out, multiplexer_1_out, multiplexer_2_out, multiplexer_3_out,
       multiplexer_4_out, multiplexer_5_out, not_1_out, not_2_out, not_3_out, not_4_out, not_5_out,
       not_6_out, not_7_out, not_8_out, not_9_out, not_10_out, not_11_out, not_12_out, not_13_out,
       not_14_out, not_15_out, not_16_out, not_17_out, not_18_out, not_19_out, or_1_out, or_2_out, or_6_out;

  or or_1 (or_1_out, A3, A2);
  Multiplexer #(.enable("false")) multiplexer_1 (.in0(A3), .in1(bitselector_1_out), .out(multiplexer_1_out), .sel(mux));
  Multiplexer #(.enable("false")) multiplexer_2 (.in0(A2), .in1(bitselector_2_out), .out(multiplexer_2_out), .sel(mux));
  BitSelector #(.width(4)) bitselector_1 (.in(B), .out(bitselector_1_out), .sel(2'b11));
  BitSelector #(.width(4)) bitselector_2 (.in(B), .out(bitselector_2_out), .sel(2'b10));
  BitSelector #(.width(4)) bitselector_3 (.in(B), .out(bitselector_3_out), .sel(2'b01));
  BitSelector #(.width(4)) bitselector_4 (.in(B), .out(bitselector_4_out), .sel(2'b00));
  Multiplexer #(.enable("false")) multiplexer_3 (.in0(A0), .in1(bitselector_4_out), .out(multiplexer_3_out), .sel(mux));
  Multiplexer #(.enable("false")) multiplexer_4 (.in0(A1), .in1(bitselector_3_out), .out(multiplexer_4_out), .sel(mux));
  Bateria_remix bateria_remix_1 (
    .Carga(or_6_out), .B3(multiplexer_1_out), .B2(multiplexer_2_out), .B1(multiplexer_4_out),
    .B0(multiplexer_3_out), .C3(D3), .C2(D2), .C1(D1), .C0(D0));
  or or_2 (or_2_out, bitselector_1_out, bitselector_2_out);
  Multiplexer #(.enable("false")) multiplexer_5 (.in0(or_1_out), .in1(or_2_out), .out(multiplexer_5_out), .sel(mux));
  not not_1 (not_1_out, multiplexer_5_out);
  not not_2 (not_2_out, El);
  not not_3 (not_3_out, Cr);
  not not_4 (not_4_out, Cf);
  not not_5 (not_5_out, El);
  not not_6 (not_6_out, Cr);
  not not_7 (not_7_out, multiplexer_5_out);
  not not_8 (not_8_out, El);
  not not_9 (not_9_out, Cf);
  not not_10 (not_10_out, El);
  not not_11 (not_11_out, El);
  not not_12 (not_12_out, multiplexer_5_out);
  not not_13 (not_13_out, Er);
  not not_14 (not_14_out, Cf);
  not not_15 (not_15_out, multiplexer_5_out);
  not not_16 (not_16_out, Er);
  not not_17 (not_17_out, Er);
  not not_18 (not_18_out, Ef);
  not not_19 (not_19_out, Ef);
  and and_1 (and_1_out, not_1_out, not_2_out, Cl, not_3_out, not_4_out);
  and and_2 (and_2_out, not_5_out, Ef, Cl, not_6_out);
  and and_3 (and_3_out, not_7_out, not_8_out, Er, Cl, not_9_out);
  and and_4 (and_4_out, not_10_out, Er, Ef, Cl);
  and and_5 (and_5_out, multiplexer_5_out, not_11_out, Ef);
  and and_6 (and_6_out, not_12_out, not_13_out, Cr, not_14_out);
  and and_7 (and_7_out, not_15_out, not_16_out, Ef, Cr);
  and and_8 (and_8_out, multiplexer_5_out, El, not_17_out, Ef);
  and and_9 (and_9_out, not_18_out, Cf);
  and and_10 (and_10_out, multiplexer_5_out, not_19_out);
  or or_3 (L, and_1_out, and_2_out, and_3_out, and_4_out, and_5_out);
  or or_4 (R, and_6_out, and_7_out, and_8_out);
  or or_5 (F, and_9_out, and_10_out);
  or or_6 (or_6_out, and_11_out, and_12_out, and_13_out);
  and and_11 (and_11_out, Cl, L);
  and and_12 (and_12_out, Cr, R);
  and and_13 (and_13_out, F, Cf);
endmodule

// RESTADOR
module Bateria_remix (
  input  Carga,
  input  B3,
  input  B2,
  input  B1,
  input  B0,
  output C3,
  output C2,
  output C1,
  output C0
);

  wire and_1_out, and_2_out, and_3_out, and_4_out, and_5_out, and_6_out, and_7_out, and_8_out, and_9_out,
       and_10_out, and_11_out, and_12_out, not_1_out, not_2_out, not_3_out, not_4_out, not_5_out, not_6_out,
       not_7_out, not_8_out, not_9_out, not_10_out;

  and and_1 (and_1_out, B3, B0);
  and and_2 (and_2_out, B3, B1);
  and and_3 (and_3_out, B3, B2);
  not not_1 (not_1_out, B2);
  not not_2 (not_2_out, B1);
  not not_3 (not_3_out, B0);
  not not_4 (not_4_out, B1);
  not not_5 (not_5_out, B0);
  not not_6 (not_6_out, B1);
  not not_7 (not_7_out, B0);
  not not_8 (not_8_out, B0);
  not not_9 (not_9_out, B0);
  not not_10 (not_10_out, B0);
  or or_1 (C3, and_1_out, and_2_out, and_3_out, Carga);
  and and_4 (and_4_out, B2, B0);
  and and_5 (and_5_out, B2, B1);
  and and_6 (and_6_out, B3, not_1_out, not_2_out, not_3_out);
  and and_7 (and_7_out, B1, B0);
  and and_8 (and_8_out, B2, not_4_out, not_5_out);
  and and_9 (and_9_out, B3, not_6_out, not_7_out);
  and and_10 (and_10_out, B1, not_8_out);
  and and_11 (and_11_out, B2, not_9_out);
  and and_12 (and_12_out, B3, not_10_out);
  or or_2 (C2, and_4_out, and_5_out, and_6_out, Carga);
  or or_3 (C1, and_7_out, and_8_out, and_9_out, Carga);
  or or_4 (C0, and_10_out, and_11_out, and_12_out, Carga);
endmodule
