// Logisim project Tarea2_CircSecuencial.circ as structural Verilog: 8 circuits, main circuit main
module main (
  input  [3:0] B
);

  wire and_1_out, bitselector_1_out, bitselector_2_out, not_1_out, not_2_out;

  not not_1 (not_1_out, bitselector_1_out);
  BitSelector #(.width(4)) bitselector_1 (.in(B), .out(bitselector_1_out), .sel(2'b11));
  BitSelector #(.width(4)) bitselector_2 (.in(B), .out(bitselector_2_out), .sel(2'b10));
  not not_2 (not_2_out, bitselector_2_out);
  and and_1 (and_1_out, not_1_out, not_2_out);
  _6_bit_Register u_6_bit_register_1 ();  // open: CLK, D0, D1, D2, D3, D4, D5, Q0, Q1, Q2, Q3, Q4, Q5
  Full_adder full_adder_1 ();  // open: A, B, Cin, S, Cout
endmodule

module SR_Latch (
  input  R,
  input  S,
  output Q,
  output nQ
);

  nor nor_1 (Q, R, nQ);
  nor nor_2 (nQ, Q, S);
endmodule

module D_Latch (
  input  CLK,
  input  D,
  output Q,
  output nQ
);

  wire and_1_out, and_2_out, not_1_out;

  not not_1 (not_1_out, D);
  and and_1 (and_1_out, CLK, not_1_out);
  and and_2 (and_2_out, CLK, D);
  SR_Latch sr_latch_1 (.R(and_1_out), .S(and_2_out), .Q(Q), .nQ(nQ));
endmodule

module D_Flip_Flop (
  input  CLK,
  input  D,
  output Q,
  output nQ
);

  wire d_latch_1_q, not_1_out;

  not not_1 (not_1_out, CLK);
  D_Latch d_latch_1 (.CLK(not_1_out), .D(D), .Q(d_latch_1_q));  // open: nQ
  D_Latch d_latch_2 (.CLK(CLK), .D(d_latch_1_q), .Q(Q), .nQ(nQ));
endmodule

module _6_bit_Register (
  input  CLK,
  input  D0,
  input  D1,
  input  D2,
  input  D3,
  input  D4,
  input  D5,
  output Q0,
  output Q1,
  output Q2,
  output Q3,
  output Q4,
  output Q5
);

  D_Flip_Flop d_flip_flop_1 (.CLK(CLK), .D(D0), .Q(Q0));  // open: nQ
  D_Flip_Flop d_flip_flop_2 (.CLK(CLK), .D(D1), .Q(Q1));  // open: nQ
  D_Flip_Flop d_flip_flop_3 (.CLK(CLK), .D(D2), .Q(Q2));  // open: nQ
  D_Flip_Flop d_flip_flop_4 (.CLK(CLK), .D(D3), .Q(Q3));  // open: nQ
  D_Flip_Flop d_flip_flop_5 (.CLK(CLK), .D(D4), .Q(Q4));  // open: nQ
  D_Flip_Flop d_flip_flop_6 (.CLK(CLK), .D(D5), .Q(Q5));  // open: nQ
endmodule

module Full_adder (
  input  A,
  input  B,
  input  Cin,
  output S,
  output Cout
);

  wire and_1_out, and_2_out, and_3_out;

  and and_1 (and_1_out, A, B);
  and and_2 (and_2_out, A, Cin);
  and and_3 (and_3_out, B, Cin);
  ExactlyOne xor_1 (.out(S), .in0(A), .in1(B), .in2(Cin));
  or or_1 (Cout, and_1_out, and_2_out, and_3_out);
endmodule

module _4bit_substractor (
  input  B3,
  input  A3,
  input  B2,
  input  A2,
  input  B1,
  input  A1,
  input  B0,
  input  A0,
  input  in_9,
  output Cout,
  output S3,
  output S2,
  output S1,
  output S0
);

  wire full_adder_2_cout, full_adder_3_cout, full_adder_4_cout, not_1_out, not_2_out, not_3_out, not_4_out;

  not not_1 (not_1_out, B3);
  Full_adder full_adder_1 (.A(A3), .B(not_1_out), .Cin(full_adder_2_cout), .S(S3), .Cout(Cout));
  not not_2 (not_2_out, B2);
  Full_adder full_adder_2 (.A(A2), .B(not_2_out), .Cin(full_adder_3_cout), .S(S2), .Cout(full_adder_2_cout));
  not not_3 (not_3_out, B1);
  Full_adder full_adder_3 (.A(A1), .B(not_3_out), .Cin(full_adder_4_cout), .S(S1), .Cout(full_adder_3_cout));
  not not_4 (not_4_out, B0);
  Full_adder full_adder_4 (.A(A0), .B(not_4_out), .Cin(in_9), .S(S0), .Cout(full_adder_4_cout));
endmodule

module TEST (
  output out_1,
  output out_2,
  output out_3,
  output out_4
);

  // _4bit_substractor 4bit_substractor_1: pin names not known; wires that end beside it: out_1, out_2
endmodule
