// Logisim project aa.circ as structural Verilog
module SR_Latch (
  input  R,
  input  S,
  output Q,
  output nQ
);

  nor nor_1 (Q, R, nQ);
  nor nor_2 (nQ, Q, S);
endmodule

module D_Latch (
  input  CLK,
  input  D,
  output Q,
  output nQ
);

  wire and_1_out, and_2_out, not_1_out;

  not not_1 (not_1_out, D);
  and and_1 (and_1_out, CLK, not_1_out);
  and and_2 (and_2_out, CLK, D);
  SR_Latch sr_latch_1 (.R(and_1_out), .S(and_2_out), .Q(Q), .nQ(nQ));
endmodule

module D_Flip_Flop (
  input  CLK,
  input  D,
  output Q,
  output nQ
);

  wire d_latch_1_q, not_1_out;

  not not_1 (not_1_out, CLK);
  D_Latch d_latch_1 (.CLK(not_1_out), .D(D), .Q(d_latch_1_q));  // open: nQ
  D_Latch d_latch_2 (.CLK(CLK), .D(d_latch_1_q), .Q(Q), .nQ(nQ));
endmodule

module _6_bit_Register (
  input  CLK,
  input  in_2,
  input  in_3,
  input  in_4,
  input  in_5,
  input  in_6,
  input  in_7,
  output out_8,
  output out_9,
  output out_10,
  output out_11,
  output out_12,
  output out_13
);

  D_Flip_Flop d_flip_flop_1 (.CLK(CLK), .D(in_2), .Q(out_8));  // open: nQ
  D_Flip_Flop d_flip_flop_2 (.CLK(CLK), .D(in_3), .Q(out_9));  // open: nQ
  D_Flip_Flop d_flip_flop_3 (.CLK(CLK), .D(in_4), .Q(out_10));  // open: nQ
  D_Flip_Flop d_flip_flop_4 (.CLK(CLK), .D(in_5), .Q(out_11));  // open: nQ
  D_Flip_Flop d_flip_flop_5 (.CLK(CLK), .D(in_6), .Q(out_12));  // open: nQ
  D_Flip_Flop d_flip_flop_6 (.CLK(CLK), .D(in_7), .Q(out_13));  // open: nQ
endmodule
